// Logisim project Projeto.circ as structural Verilog: 1 circuit, main circuit main
module main (
  input  in_1,
  output [7:0] out_2
);

  wire and_1_out, and_2_out, and_3_out, and_4_out, and_5_out, and_6_out, and_7_out, and_8_out, and_9_out,
       and_10_out, and_11_out, and_12_out, and_13_out, and_14_out, and_15_out, and_19_out, and_20_out,
       and_21_out, and_22_out, and_23_out, c, not_1_out, not_2_out, not_3_out, not_4_out, not_5_out,
       not_6_out, not_7_out, not_8_out, pulso2, pulso4, pulso6, pulso8;

  not not_1 (not_1_out, out_2[0]);
  and and_1 (and_1_out, in_1, not_1_out);
  and and_2 (and_2_out, in_1, out_2[0]);
  not not_2 (not_2_out, out_2[2]);
  and and_3 (and_3_out, pulso2, not_2_out);
  and and_4 (and_4_out, out_2[2], pulso2);
  not not_3 (not_3_out, out_2[4]);
  and and_5 (and_5_out, pulso4, not_3_out);
  and and_6 (and_6_out, out_2[4], pulso4);
  J_K_Flip_Flop j_k_ff_1 (.J(and_1_out), .clk(c), .K(and_2_out), .Q(out_2[0]));  // open: Qn, preset, en, reset
  J_K_Flip_Flop j_k_ff_2 (.J(and_3_out), .clk(c), .K(and_4_out), .Q(out_2[2]));  // open: Qn, preset, en, reset
  J_K_Flip_Flop j_k_ff_3 (.J(and_5_out), .clk(c), .K(and_6_out), .Q(out_2[4]));  // open: Qn, preset, en, reset
  Clock clock_1 (.out(c));
  and and_7 (and_7_out, in_1, out_2[0]);
  not not_4 (not_4_out, out_2[1]);
  and and_8 (and_8_out, and_7_out, not_4_out);
  and and_9 (and_9_out, out_2[1], and_7_out);
  and and_10 (and_10_out, pulso2, out_2[2]);
  not not_5 (not_5_out, out_2[3]);
  and and_11 (and_11_out, and_10_out, not_5_out);
  and and_12 (and_12_out, pulso4, out_2[4]);
  not not_6 (not_6_out, out_2[5]);
  and and_13 (and_13_out, and_12_out, not_6_out);
  J_K_Flip_Flop j_k_ff_4 (.J(and_8_out), .clk(c), .K(and_9_out), .Q(out_2[1]));  // open: Qn, preset, en, reset
  and and_14 (and_14_out, out_2[3], and_10_out);
  J_K_Flip_Flop j_k_ff_5 (.J(and_11_out), .clk(c), .K(and_14_out), .Q(out_2[3]));  // open: Qn, preset, en, reset
  and and_15 (and_15_out, out_2[5], and_12_out);
  J_K_Flip_Flop j_k_ff_6 (.J(and_13_out), .clk(c), .K(and_15_out), .Q(out_2[5]));  // open: Qn, preset, en, reset
  and and_16 (pulso2, and_7_out, out_2[1]);
  and and_17 (pulso4, and_10_out, out_2[3]);
  and and_18 (pulso6, and_12_out, out_2[5]);
  not not_7 (not_7_out, out_2[6]);
  and and_19 (and_19_out, pulso6, not_7_out);
  and and_20 (and_20_out, out_2[6], pulso6);
  J_K_Flip_Flop j_k_ff_7 (.J(and_19_out), .clk(c), .K(and_20_out), .Q(out_2[6]));  // open: Qn, preset, en, reset
  and and_21 (and_21_out, pulso6, out_2[6]);
  not not_8 (not_8_out, out_2[7]);
  and and_22 (and_22_out, and_21_out, not_8_out);
  and and_23 (and_23_out, out_2[7], and_21_out);
  J_K_Flip_Flop j_k_ff_8 (.J(and_22_out), .clk(c), .K(and_23_out), .Q(out_2[7]));  // open: Qn, preset, en, reset
  and and_24 (pulso8, and_21_out, out_2[7]);

  // Other names for the same wires on the sheet: s1 = out_2[0]; s2 = out_2[1]; s3 = out_2[2]; s4 = out_2[3];
  //   s5 = out_2[4]; s6 = out_2[5]; s7 = out_2[6]; s8 = out_2[7]
endmodule
